# Fritzing sketch 8bits-expansion (saved by Fritzing 0.9.0b)
circuit board: 4.7cm x 7.5cm
breadboards: 1

parts:
  PWR = Header 3 [package=jst-3-pth]
  CD4021 = CD4021B [package="DIP (Dual Inline) [THT]"]
  DATA_IO = shrouded pin header, 10 pins [form="♂ (shrouded male)"]
  R1 = Resistor [tolerance=±5% resistance=10k package=THT]
  R2 = Resistor [tolerance=±5% resistance=10k package=THT]
  R3 = Resistor [tolerance=±5% resistance=10k package=THT]
  R4 = Resistor [tolerance=±5% resistance=10k package=THT]
  R5 = Resistor [tolerance=±5% resistance=10k package=THT]
  IN-0 = male pin header, 2 pins [form="♂ (male)"]
  IN-1 = male pin header, 2 pins [form="♂ (male)"]
  IN-2 = male pin header, 2 pins [form="♂ (male)"]
  IN-3 = male pin header, 2 pins [form="♂ (male)"]
  IN-4 = male pin header, 2 pins [form="♂ (male)"]
  BLT = male pin header, 2 pins [form="♂ (male)"]
  R6 = Resistor [tolerance=±5% resistance=220 package=THT]
  R7 = Resistor [tolerance=±5% resistance=220 package=THT]
  R8 = Resistor [tolerance=±5% resistance=220 package=THT]
  R9 = Resistor [tolerance=±5% resistance=220 package=THT]
  OUT-0 = male pin header, 2 pins [form="♂ (male)"]
  OUT-3 = male pin header, 2 pins [form="♂ (male)"]
  OUT-1 = male pin header, 2 pins [form="♂ (male)"]
  OUT-2 = male pin header, 2 pins [form="♂ (male)"]
  74HC595 = 74HC595 [package="DIP16 [THT]"]
  R10 = Resistor [tolerance=±5% resistance=220 package=THT]
  R11 = Resistor [tolerance=±5% resistance=220 package=THT]
  R12 = Resistor [tolerance=±5% resistance=220 package=THT]
  R13 = Resistor [tolerance=±5% resistance=220 package=THT]
  OUT-4 = male pin header, 2 pins [form="♂ (male)"]
  OUT-5 = male pin header, 2 pins [form="♂ (male)"]
  OUT-6 = male pin header, 2 pins [form="♂ (male)"]
  OUT-7 = male pin header, 2 pins [form="♂ (male)"]
  IN-5 = male pin header, 2 pins [form="♂ (male)"]
  R14 = Resistor [tolerance=±5% resistance=10k package=THT]
  IN-6 = male pin header, 2 pins [form="♂ (male)"]
  R15 = Resistor [tolerance=±5% resistance=10k package=THT]
  IN-7 = male pin header, 2 pins [form="♂ (male)"]
  R16 = Resistor [tolerance=±5% resistance=10k package=THT]
  S-INPUT = male pin header, 3 pins [form="♂ (male)"]
  S-OUTPUT = male pin header, 3 pins [form="♂ (male)"]
  ANALOG-0 = male pin header, 3 pins [form="♂ (male)"]
  ANALOG-1 = male pin header, 3 pins [form="♂ (male)"]
  ANALOG-2 = male pin header, 3 pins [form="♂ (male)"]
  ANALOG-3 = male pin header, 3 pins [form="♂ (male)"]

nets:
  5V: PWR.1, CD4021.VDD, IN-0.pin1, IN-1.pin1, IN-2.pin1, IN-3.pin1, IN-4.pin1, 74HC595.MR, 74HC595.VCC, IN-5.pin1, IN-6.pin1, IN-7.pin1, ANALOG-0.pin1, ANALOG-1.pin1, ANALOG-2.pin1, ANALOG-3.pin1
  GND: PWR.2, CD4021.VSS, R1.Pin_0, R2.Pin_0, R3.Pin_0, R4.Pin_0, R5.Pin_0, BLT.pin2, R6.Pin_0, R7.Pin_0, R8.Pin_0, R9.Pin_0, 74HC595.GND, 74HC595.OE, R10.Pin_0, R11.Pin_0, R12.Pin_0, R13.Pin_0, R14.Pin_0, R15.Pin_0, R16.Pin_0, ANALOG-0.pin3, ANALOG-1.pin3, ANALOG-2.pin3, ANALOG-3.pin3
  12V: PWR.3, BLT.pin1
  N1: CD4021.PI8, IN-7.pin2, R16.Pin_1
  N2: CD4021.Q8, DATA_IO.pin3
  N3: CD4021.PI4, R4.Pin_1, IN-3.pin2
  N4: CD4021.PI3, R3.Pin_1, IN-2.pin2
  N5: CD4021.PI2, R2.Pin_1, IN-1.pin2
  N6: CD4021.PI1, R1.Pin_1, IN-0.pin2
  N7: CD4021.PSC, DATA_IO.pin2, S-INPUT.pin2
  N8: CD4021.CLK, DATA_IO.pin1, S-INPUT.pin1
  N9: CD4021.SIN, S-INPUT.pin3
  N10: CD4021.PI5, R5.Pin_1, IN-4.pin2
  N11: CD4021.PI6, IN-5.pin2, R14.Pin_1
  N12: CD4021.PI7, IN-6.pin2, R15.Pin_1
  N13: DATA_IO.pin4, 74HC595.SH_CP, S-OUTPUT.pin1
  N14: DATA_IO.pin5, 74HC595.ST_CP, S-OUTPUT.pin2
  N15: DATA_IO.pin6, 74HC595.DS
  N16: DATA_IO.pin7, ANALOG-0.pin2
  N17: DATA_IO.pin8, ANALOG-1.pin2
  N18: DATA_IO.pin9, ANALOG-2.pin2
  N19: DATA_IO.pin10, ANALOG-3.pin2
  N20: R6.Pin_1, OUT-0.pin2
  N21: R7.Pin_1, OUT-1.pin2
  N22: R8.Pin_1, OUT-3.pin2
  N23: R9.Pin_1, OUT-2.pin2
  N24: OUT-0.pin1, 74HC595.Q0
  N25: OUT-3.pin1, 74HC595.Q3
  N26: OUT-1.pin1, 74HC595.Q1
  N27: OUT-2.pin1, 74HC595.Q2
  N28: 74HC595.Q4, OUT-4.pin1
  N29: 74HC595.Q5, OUT-5.pin1
  N30: 74HC595.Q6, OUT-6.pin1
  N31: 74HC595.Q7, OUT-7.pin1
  N32: 74HC595.Q7', S-OUTPUT.pin3
  N33: R10.Pin_1, OUT-6.pin2
  N34: R11.Pin_1, OUT-7.pin2
  N35: R12.Pin_1, OUT-5.pin2
  N36: R13.Pin_1, OUT-4.pin2

notes:
  Open Airbus Cockpit
  8-Bits Expansion Card
  Rev. 02
  By Alvaro Polo

custom parts:
  CD4021B: Asynchronous Parallel Input or Synchronous Serial Input/Serial Output
