# Fritzing sketch keypad (saved by Fritzing 0.9.0b)
circuit board: 4.5cm x 6.5cm
breadboards: 1

parts:
  74C922N-1 = DIP - 18 pins [chip_label=74C922N package="DIP (Dual Inline) [THT]"]
  SW1-11 = male pin header, 2 pins [form="♂ (male)"]
  SW-1-21 = male pin header, 2 pins [form="♂ (male)"]
  SW-1-31 = male pin header, 2 pins [form="♂ (male)"]
  SW-1-41 = male pin header, 2 pins [form="♂ (male)"]
  SW-1-22 = male pin header, 2 pins [form="♂ (male)"]
  SW-1-12 = male pin header, 2 pins [form="♂ (male)"]
  SW-1-32 = male pin header, 2 pins [form="♂ (male)"]
  SW-1-42 = male pin header, 2 pins [form="♂ (male)"]
  SW-1-13 = male pin header, 2 pins [form="♂ (male)"]
  SW-1-43 = male pin header, 2 pins [form="♂ (male)"]
  SW-1-23 = male pin header, 2 pins [form="♂ (male)"]
  SW-1-24 = male pin header, 2 pins [form="♂ (male)"]
  SW-1-34 = male pin header, 2 pins [form="♂ (male)"]
  SW-1-33 = male pin header, 2 pins [form="♂ (male)"]
  SW-1-14 = male pin header, 2 pins [form="♂ (male)"]
  SW-1-44 = male pin header, 2 pins [form="♂ (male)"]
  DATA-BUS = male pin header, 4 pins [form="♂ (male)"]
  CTRL-1 = male pin header, 2 pins [form="♂ (male)"]
  PWR = male pin header, 2 pins [form="♂ (male)"]
  74C922N-2 = DIP - 18 pins [chip_label=74C922N package="DIP (Dual Inline) [THT]"]
  SW-2-23 = male pin header, 2 pins [form="♂ (male)"]
  SW-2-43 = male pin header, 2 pins [form="♂ (male)"]
  SW-2-33 = male pin header, 2 pins [form="♂ (male)"]
  SW-2-21 = male pin header, 2 pins [form="♂ (male)"]
  SW-2-22 = male pin header, 2 pins [form="♂ (male)"]
  SW-2-42 = male pin header, 2 pins [form="♂ (male)"]
  SW-2-24 = male pin header, 2 pins [form="♂ (male)"]
  SW-2-13 = male pin header, 2 pins [form="♂ (male)"]
  SW-2-34 = male pin header, 2 pins [form="♂ (male)"]
  SW-2-32 = male pin header, 2 pins [form="♂ (male)"]
  SW-2-31 = male pin header, 2 pins [form="♂ (male)"]
  SW-2-41 = male pin header, 2 pins [form="♂ (male)"]
  SW-2-12 = male pin header, 2 pins [form="♂ (male)"]
  SW-2-14 = male pin header, 2 pins [form="♂ (male)"]
  SW-2-44 = male pin header, 2 pins [form="♂ (male)"]
  SW-2-11 = male pin header, 2 pins [form="♂ (male)"]
  CTRL-2 = male pin header, 2 pins [form="♂ (male)"]
  DATA-BUS-LINK = male pin header, 4 pins [form="♂ (male)"]
  KEYB-1 = Ceramic Capacitor [capacitance=0.1µF package="100 mil [THT, multilayer]"]
  OSC-1 = Ceramic Capacitor [capacitance=0.1µF package="100 mil [THT, multilayer]"]
  KEYB-2 = Ceramic Capacitor [capacitance=0.1µF package="100 mil [THT, multilayer]"]
  OSC-2 = Ceramic Capacitor [capacitance=0.1µF package="100 mil [THT, multilayer]"]
  PWR-LINK = male pin header, 2 pins [form="♂ (male)"]

nets:
  N1: 74C922N-1.ROW-Y1, SW1-11.pin2, SW-1-21.pin2, SW-1-31.pin2, SW-1-41.pin2
  N2: 74C922N-1.ROW-Y2, SW-1-22.pin2, SW-1-12.pin2, SW-1-32.pin2, SW-1-42.pin2
  N3: 74C922N-1.ROW-Y3, SW-1-13.pin2, SW-1-43.pin2, SW-1-23.pin2, SW-1-33.pin2
  N4: 74C922N-1.ROW-Y4, SW-1-24.pin2, SW-1-34.pin2, SW-1-14.pin2, SW-1-44.pin2
  N5: 74C922N-1.OSCIL, OSC-1.0
  N6: 74C922N-1.KEYB, KEYB-1.0
  N7: 74C922N-1.COL-X4, SW-1-41.pin1, SW-1-42.pin1, SW-1-43.pin1, SW-1-44.pin1
  N8: 74C922N-1.COL-X3, SW-1-31.pin1, SW-1-32.pin1, SW-1-34.pin1, SW-1-33.pin1
  GND: 74C922N-1.GND, PWR.pin2, 74C922N-2.GND, KEYB-1.1, OSC-1.1, KEYB-2.1, OSC-2.1, PWR-LINK.pin2
  N9: 74C922N-1.COL-X2, SW-1-21.pin1, SW-1-22.pin1, SW-1-23.pin1, SW-1-24.pin1
  N10: 74C922N-1.COL-X1, SW1-11.pin1, SW-1-12.pin1, SW-1-13.pin1, SW-1-14.pin1
  N11: 74C922N-1.DAV, CTRL-1.pin1
  N12: 74C922N-1.OE, CTRL-1.pin2
  N13: 74C922N-1.D, DATA-BUS.pin4, 74C922N-2.D, DATA-BUS-LINK.pin4
  N14: 74C922N-1.C, DATA-BUS.pin3, 74C922N-2.C, DATA-BUS-LINK.pin3
  N15: 74C922N-1.B, DATA-BUS.pin2, 74C922N-2.B, DATA-BUS-LINK.pin2
  N16: 74C922N-1.A, DATA-BUS.pin1, 74C922N-2.A, DATA-BUS-LINK.pin1
  5V: 74C922N-1.VCC, PWR.pin1, 74C922N-2.VCC, PWR-LINK.pin1
  N17: 74C922N-2.ROW-Y1, SW-2-21.pin2, SW-2-31.pin2, SW-2-41.pin2, SW-2-11.pin2
  N18: 74C922N-2.ROW-Y2, SW-2-22.pin2, SW-2-42.pin2, SW-2-32.pin2, SW-2-12.pin2
  N19: 74C922N-2.ROW-Y3, SW-2-23.pin2, SW-2-43.pin2, SW-2-33.pin2, SW-2-13.pin2
  N20: 74C922N-2.ROW-Y4, SW-2-24.pin2, SW-2-34.pin2, SW-2-14.pin2, SW-2-44.pin2
  N21: 74C922N-2.OSCIL, OSC-2.0
  N22: 74C922N-2.KEYB, KEYB-2.0
  N23: 74C922N-2.COL-X4, SW-2-43.pin1, SW-2-42.pin1, SW-2-41.pin1, SW-2-44.pin1
  N24: 74C922N-2.COL-X3, SW-2-33.pin1, SW-2-34.pin1, SW-2-32.pin1, SW-2-31.pin1
  N25: 74C922N-2.COL-X2, SW-2-23.pin1, SW-2-21.pin1, SW-2-22.pin1, SW-2-24.pin1
  N26: 74C922N-2.COL-X1, SW-2-13.pin1, SW-2-12.pin1, SW-2-14.pin1, SW-2-11.pin1
  N27: 74C922N-2.DAV, CTRL-2.pin1
  N28: 74C922N-2.OE, CTRL-2.pin2

notes:
  VCC
  GND
  DAV
  OE
  Open Airbus Cockpit
  Keypad Expansion Card
  By Alvaro Polo  Rev. 02

custom parts:
  DIP - 18 pins: A DIP stand-in part for whatever IC you want. With 18 pins on a 300mil dual inline package (DIP) footprint.
